# Fritzing sketch GPS_BME280_OLED_NEW_Fritzing (saved by Fritzing 0.9.4)
circuit board: 8.46667cm x 5.64444cm
breadboards: 1

parts:
  Bauteil1 = Arduino Nano (Rev3.0)
  Bauteil2 = GY-BMEP280 Barometric Pressure Sensor - Breakout  # not connected
  Hybrid_Circuit1 = JY-MCU 3V-5V Bidirectional Level Shifter [package="DIP (Dual Inline)"]
  Bauteil3 = u-blox NEO-6M GPS Breakout
  OLED1 = OLED 128x64 I2C Monochrome Display
  SD_card_module1 = SD Card Module  # not connected

nets:
  GND: Bauteil1.GND, Hybrid_Circuit1.3.3Vout, Hybrid_Circuit1.5Vin, Bauteil3.GND, OLED1.GND
  N1: Bauteil1.D4, Bauteil3.TXD
  5V: Bauteil1.5V, Hybrid_Circuit1.I/O-4H, Bauteil3.VCC
  N2: Bauteil1.A5, Hybrid_Circuit1.I/O-2H
  N3: Bauteil1.A4, Hybrid_Circuit1.I/O-3H
  3V3: Bauteil1.3V3, Hybrid_Circuit1.I/O-4L, Bauteil3.PPS, OLED1.VDD
  N4: Hybrid_Circuit1.I/O-1L, OLED1.SDA
  N5: Hybrid_Circuit1.I/O-2L, OLED1.SCK

custom parts:
  GY-BMEP280 Barometric Pressure Sensor - Breakout: The BME280 is a chip which was originally designed for the next generation of smartphones. It is made up of a very accurate pressure sensor and an associated temperature sensor which helps calibrate the pressure readings. And just for fun they threw in a pretty solid humidity sensor in there as well! So with an I2C connection you have access to enough weather data to make some pretty good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
  JY-MCU 3V-5V Bidirectional Level Shifter: JY-MCU 3V-5V Bidirectional Level Shifter with 12 pins on a 500mil dual inline package (DIP) footprint.
  SD Card Module: SD Card Module Slot Socket Reader For Arduino ARM MCU
